// Logisim project processor.circ as structural Verilog: 4 circuits, main circuit Processor-Pipeline
module Register_File (
  input  Clock,
  input  [4:0] Select_RC,
  input  [4:0] Select_RA,
  input  [4:0] Select_RB,
  input  [31:0] Input_RC,
  input  Clear_RF,
  input  En_Select_RC,
  input  En_Select_RA,
  input  En_Select_RB,
  output [31:0] RA,
  output [31:0] RB
);

  wire En0, En1, En2, En3, En4, En5, En6, En7, En8, En9, En10, En11, En12, En13, En14, En15, En16, En17,
       En18, En19, En20, En21, En22, En23, En24, En25, En26, En27, En28, En29, En30, En31;
  wire [31:0] O0, O1, O2, O3, O4, O5, O6, O7, O8, O9, O10, O11, O12, O13, O14, O15, O16, O17, O18, O19, O20,
       O21, O22, O23, O24, O25, O26, O27, O28, O29, O30, O31;

  // Probe on O0
  // Probe on O8
  // Probe on O16
  // Probe on O24
  Register #(.width(32)) R0 (.D(Input_RC), .en(En0), .Q(O0), .clk(Clock), .clr(Clear_RF));
  Register #(.width(32)) R8 (.D(Input_RC), .en(En8), .Q(O8), .clk(Clock), .clr(Clear_RF));
  Register #(.width(32)) R16 (.D(Input_RC), .en(En16), .Q(O16), .clk(Clock), .clr(Clear_RF));
  Register #(.width(32)) R24 (.D(Input_RC), .en(En24), .Q(O24), .clk(Clock), .clr(Clear_RF));
  Register #(.width(32)) R1 (.D(Input_RC), .en(En1), .Q(O1), .clk(Clock), .clr(Clear_RF));
  Register #(.width(32)) R9 (.D(Input_RC), .en(En9), .Q(O9), .clk(Clock), .clr(Clear_RF));
  Register #(.width(32)) R17 (.D(Input_RC), .en(En17), .Q(O17), .clk(Clock), .clr(Clear_RF));
  Register #(.width(32)) R25 (.D(Input_RC), .en(En25), .Q(O25), .clk(Clock), .clr(Clear_RF));
  // Probe on O1
  // Probe on O9
  // Probe on O17
  // Probe on O25
  Demultiplexer #(.select(5), .disabled(0)) demultiplexer_1 (
    .out0(En0), .out1(En1), .out2(En2), .out3(En3), .out4(En4), .out5(En5), .out6(En6), .out7(En7),
    .out8(En8), .out9(En9), .out10(En10), .out11(En11), .out12(En12), .out13(En13), .out14(En14),
    .out15(En15), .out16(En16), .out17(En17), .out18(En18), .out19(En19), .out20(En20), .out21(En21),
    .out22(En22), .out23(En23), .out24(En24), .out25(En25), .out26(En26), .out27(En27), .out28(En28),
    .out29(En29), .out30(En30), .out31(En31), .in(1'b1), .sel(Select_RC), .en(En_Select_RC));
  // Probe on O2
  // Probe on O10
  // Probe on O18
  // Probe on O26
  Register #(.width(32)) R2 (.D(Input_RC), .en(En2), .Q(O2), .clk(Clock), .clr(Clear_RF));
  Register #(.width(32)) R10 (.D(Input_RC), .en(En10), .Q(O10), .clk(Clock), .clr(Clear_RF));
  Register #(.width(32)) R18 (.D(Input_RC), .en(En18), .Q(O18), .clk(Clock), .clr(Clear_RF));
  Register #(.width(32)) R26 (.D(Input_RC), .en(En26), .Q(O26), .clk(Clock), .clr(Clear_RF));
  Register #(.width(32)) R3 (.D(Input_RC), .en(En3), .Q(O3), .clk(Clock), .clr(Clear_RF));
  Register #(.width(32)) R11 (.D(Input_RC), .en(En11), .Q(O11), .clk(Clock), .clr(Clear_RF));
  Register #(.width(32)) R19 (.D(Input_RC), .en(En19), .Q(O19), .clk(Clock), .clr(Clear_RF));
  Register #(.width(32)) R27 (.D(Input_RC), .en(En27), .Q(O27), .clk(Clock), .clr(Clear_RF));
  // Probe on O3
  // Probe on O11
  // Probe on O19
  // Probe on O27
  // Probe on Select_RA
  // Probe on O4
  // Probe on O12
  // Probe on O20
  // Probe on O28
  Register #(.width(32)) R4 (.D(Input_RC), .en(En4), .Q(O4), .clk(Clock), .clr(Clear_RF));
  Register #(.width(32)) R12 (.D(Input_RC), .en(En12), .Q(O12), .clk(Clock), .clr(Clear_RF));
  Register #(.width(32)) R20 (.D(Input_RC), .en(En20), .Q(O20), .clk(Clock), .clr(Clear_RF));
  Register #(.width(32)) R28 (.D(Input_RC), .en(En28), .Q(O28), .clk(Clock), .clr(Clear_RF));
  // Probe on RA
  Multiplexer #(.select(5), .width(32), .disabled(0)) multiplexer_1 (
    .in0(O0), .in1(O1), .in2(O2), .in3(O3), .in4(O4), .in5(O5), .in6(O6), .in7(O7), .in8(O8), .in9(O9),
    .in10(O10), .in11(O11), .in12(O12), .in13(O13), .in14(O14), .in15(O15), .in16(O16), .in17(O17),
    .in18(O18), .in19(O19), .in20(O20), .in21(O21), .in22(O22), .in23(O23), .in24(O24), .in25(O25),
    .in26(O26), .in27(O27), .in28(O28), .in29(O29), .in30(O30), .in31(O31), .out(RA), .sel(Select_RA),
    .en(En_Select_RA));
  Register #(.width(32)) R5 (.D(Input_RC), .en(En5), .Q(O5), .clk(Clock), .clr(Clear_RF));
  Register #(.width(32)) R13 (.D(Input_RC), .en(En13), .Q(O13), .clk(Clock), .clr(Clear_RF));
  Register #(.width(32)) R21 (.D(Input_RC), .en(En21), .Q(O21), .clk(Clock), .clr(Clear_RF));
  Register #(.width(32)) R29 (.D(Input_RC), .en(En29), .Q(O29), .clk(Clock), .clr(Clear_RF));
  // Probe on O5
  // Probe on O13
  // Probe on O21
  // Probe on O29
  // Probe on O6
  // Probe on O14
  // Probe on O22
  // Probe on O30
  // Probe on Select_RB
  Register #(.width(32)) R6 (.D(Input_RC), .en(En6), .Q(O6), .clk(Clock), .clr(Clear_RF));
  Register #(.width(32)) R14 (.D(Input_RC), .en(En14), .Q(O14), .clk(Clock), .clr(Clear_RF));
  Register #(.width(32)) R22 (.D(Input_RC), .en(En22), .Q(O22), .clk(Clock), .clr(Clear_RF));
  Register #(.width(32)) R30 (.D(Input_RC), .en(En30), .Q(O30), .clk(Clock), .clr(Clear_RF));
  Multiplexer #(.select(5), .width(32), .disabled(0)) multiplexer_2 (
    .in0(O0), .in1(O1), .in2(O2), .in3(O3), .in4(O4), .in5(O5), .in6(O6), .in7(O7), .in8(O8), .in9(O9),
    .in10(O10), .in11(O11), .in12(O12), .in13(O13), .in14(O14), .in15(O15), .in16(O16), .in17(O17),
    .in18(O18), .in19(O19), .in20(O20), .in21(O21), .in22(O22), .in23(O23), .in24(O24), .in25(O25),
    .in26(O26), .in27(O27), .in28(O28), .in29(O29), .in30(O30), .in31(O31), .out(RB), .sel(Select_RB),
    .en(En_Select_RB));
  Register #(.width(32)) R7 (.D(Input_RC), .en(En7), .Q(O7), .clk(Clock), .clr(Clear_RF));
  Register #(.width(32)) R15 (.D(Input_RC), .en(En15), .Q(O15), .clk(Clock), .clr(Clear_RF));
  Register #(.width(32)) R23 (.D(Input_RC), .en(En23), .Q(O23), .clk(Clock), .clr(Clear_RF));
  Register #(.width(32)) R31 (.D(Input_RC), .en(En31), .Q(O31), .clk(Clock), .clr(Clear_RF));
  // Probe on O7
  // Probe on O15
  // Probe on O23
  // Probe on O31
  // Probe on RB

  // Other names for the same wires on the sheet: Clear = Clear_RF; Input[31:0] = Input_RC
endmodule

module ALU (
  input  [31:0] In_RA,
  input  [31:0] In_MUX_B,
  input  [1:0] Select_ALU,
  input  Enable_ALU,
  output [31:0] Out_RZ
);

  wire [31:0] tunnel, tunnel_t, tunnel_t_t, x;

  Adder #(.width(32)) adder_1 (.a(In_RA), .b(In_MUX_B), .out(tunnel), .cin(1'b0));  // open: cout
  Subtractor #(.width(32)) subtractor_1 (.a(In_RA), .b(In_MUX_B), .out(tunnel_t), .bin(1'b0));  // open: bout
  Multiplier #(.width(32)) multiplier_1 (.a(In_RA), .b(In_MUX_B), .out(x), .cin({32{1'b0}}));  // open: cout
  Divider #(.width(32)) divider_1 (.a(In_RA), .b(In_MUX_B), .out(tunnel_t_t), .upper({32{1'b0}}));  // open: rem
  Multiplexer #(.select(2), .width(32)) multiplexer_1 (
    .in0(tunnel), .in1(tunnel_t), .in2(x), .in3(tunnel_t_t), .out(Out_RZ), .sel(Select_ALU), .en(Enable_ALU));

  // Other names for the same wires on the sheet: Output[31:0] = Out_RZ; RA[31:0] = In_RA; RB[31:0] = In_MUX_B
endmodule

module Processor_Pipeline (
  input  in_1,
  input  in_2
);

  wire Clear___RF, Clear_IR, Clock, clock_1_out, control_unit_1_stage_1, control_unit_1_stage_2,
       control_unit_1_stage_3, control_unit_1_stage_4, control_unit_1_stage_5, CS, En_ALU, En_IR, En_MUX_B,
       En_MUX_Y, En_PC, En_RA, En_RB, En_RM, En_RY, En_RZ, En_Select_RA, En_Select_RB, En_Select_RC,
       Enable_MUX_MA, Enable_PCSet, Enable_to_MUX_Y, Jump_Signal, Load_Signal, Load_Write_Ram, Move_Signal,
       not_1_out, Select_MUX_B, Select_MUX_MA, Select_MUX_Y, Select_PCSet, Signal, Signal_t, Store_Signal,
       Subtract_Signal, x_Signal;
  wire [1:0] Select_ALU;
  wire [2:0] Op_Code;
  wire [4:0] Select_RA, Select_RB;
  wire [17:0] Address;
  wire [18:0] Immediate;
  wire [31:0] adder_1_out, alu_1_out_rz, In_MUX_Y, Input_IR, multiplexer_1_out, multiplexer_2_out,
       multiplexer_3_out, Out_RAM, Out_RZ, PC_q, RA_q, RB_q, register_file_1_ra, register_file_1_rb, RY;
  wire [31:19] MemoryAddress;

  or or_1 (Clock, Clear_IR, clock_1_out);
  Register #(.width(32)) RA (.D(register_file_1_ra), .en(En_RA), .Q(RA_q), .clk(Clock), .clr(Clear_IR));
  // Probe on Select_ALU
  Button button_1 (.out(Clear_IR));
  Clock clock_1 (.out(clock_1_out));
  Register_File register_file_1 (
    .Clear_RF(Clear___RF), .En_Select_RC(En_Select_RC), .En_Select_RA(En_Select_RA),
    .En_Select_RB(En_Select_RB), .Select_RC(Select_RB), .Select_RA(Select_RA), .Select_RB(Select_RB),
    .RA(register_file_1_ra), .RB(register_file_1_rb), .Clock(Clock), .Input_RC(RY));
  Register #(.width(32)) RB (.D(register_file_1_rb), .en(En_RB), .Q(RB_q), .clk(Clock), .clr(Clear_IR));
  // Probe on multiplexer_1_out
  ALU alu_1 (
    .In_RA(RA_q), .In_MUX_B(multiplexer_1_out), .Out_RZ(alu_1_out_rz), .Select_ALU(Select_ALU),
    .Enable_ALU(En_ALU));
  Register #(.width(32)) RZ (.D(alu_1_out_rz), .en(En_RZ), .Q(Out_RZ), .clk(Clock), .clr(Clear_IR));
  Multiplexer #(.width(32)) multiplexer_1 (
    .in0(RB_q), .in1({{13{in_1}}, Immediate}), .out(multiplexer_1_out), .sel(Select_MUX_B), .en(En_MUX_B));
  Multiplexer #(.width(32)) multiplexer_2 (
    .in0(Out_RZ), .in1(In_MUX_Y), .out(multiplexer_2_out), .sel(Select_MUX_Y), .en(En_MUX_Y));
  Register #(.width(32)) u_RY (.D(multiplexer_2_out), .en(En_RY), .Q(RY), .clk(Clock), .clr(Clear_IR));
  Register #(.width(32)) RM (.D(RB_q), .en(En_RM), .Q(Out_RAM), .clk(Clock), .clr(Clear_IR));
  // Probe on Out_RZ
  // Probe on In_MUX_Y
  // Probe on Out_RAM
  // Probe on CS
  Register #(.width(32)) IR (
    .D(Input_IR), .en(En_IR), .Q({Op_Code, Select_RA, Select_RB, Immediate}), .clk(Clock), .clr(Clear_IR));
  Multiplexer #(.width(32)) multiplexer_3 (
    .in0({{13{in_1}}, Immediate}), .in1(adder_1_out), .out(multiplexer_3_out), .sel(Select_PCSet),
    .en(Enable_PCSet));
  // Probe on {MemoryAddress, CS, Address}
  Multiplexer #(.width(32)) multiplexer_4 (
    .in0(Input_IR), .in1(Out_RAM), .out(In_MUX_Y), .sel(CS), .en(Enable_to_MUX_Y));
  // Probe on {Op_Code, Select_RA, Select_RB, Immediate}
  // Probe on multiplexer_3_out
  Register #(.width(32)) PC (.D(multiplexer_3_out), .en(En_PC), .Q(PC_q), .clk(Clock), .clr(Clear_IR));
  // Probe on Address
  not not_1 (not_1_out, CS);
  // Probe on {{13{in_1}}, Immediate}
  Multiplexer #(.width(32)) multiplexer_5 (
    .in0(Out_RZ), .in1(PC_q), .out({MemoryAddress, CS, Address}), .sel(Select_MUX_MA), .en(Enable_MUX_MA));
  Adder #(.width(32)) adder_1 (.a(PC_q), .b(32'h1), .out(adder_1_out), .cin(in_2));  // open: cout
  RAM #(.addrWidth(18), .dataWidth(32)) ram_1 (
    .addr(Address), .data(Out_RAM), .sel(CS), .clk(Clock), .ld(Load_Write_Ram), .clr(Clear_IR));
  // Probe on adder_1_out
  // Probe on Input_IR
  ROM #(.addrWidth(18), .dataWidth(32)) rom_1 (.addr(Address), .data(Input_IR), .sel(not_1_out));
  // Probe on Out_RAM
  Decoder #(.select(3), .enable("false")) decoder_1 (
    .out0(Load_Signal), .out1(Store_Signal), .out2(Move_Signal), .out3(Jump_Signal), .out4(Signal),
    .out5(Subtract_Signal), .out6(x_Signal), .out7(Signal_t), .sel(Op_Code));
  Control_Unit control_unit_1 (
    .Load_Signal(Load_Signal), .Store_Signal(Store_Signal), .Move_Signal(Move_Signal),
    .Jump_Signal(Jump_Signal), .Signal(Signal), .Subtract_Signal(Subtract_Signal), .x_Signal(x_Signal),
    .Signal_2(Signal_t), .Clock(Clock), .En_IR(En_IR), .En_PC(En_PC), .Select_MUX_MA(Select_MUX_MA),
    .Enable_MUX_MA(Enable_MUX_MA), .Enable_PCSet(Enable_PCSet), .Select_PCSet(Select_PCSet), .En_RA(En_RA),
    .En_RB(En_RB), .En_Select_RA(En_Select_RA), .En_Select_RB(En_Select_RB), .En_RZ(En_RZ),
    .Select_ALU(Select_ALU), .En_RM(En_RM), .En_ALU(En_ALU), .Select_MUX_Y(Select_MUX_Y),
    .En_MUX_Y(En_MUX_Y), .Load_Write_Ram(Load_Write_Ram), .Enable_to_MUX_Y(Enable_to_MUX_Y), .En_RY(En_RY),
    .Op_Code(Op_Code), .En_Select_RC(En_Select_RC), .En_MUX_B(En_MUX_B), .Select_MUX_B(Select_MUX_B),
    .Load_Stage_Clk(Clear_IR), .Stage_1(control_unit_1_stage_1), .Stage_2(control_unit_1_stage_2),
    .Stage_4(control_unit_1_stage_4), .Stage_3(control_unit_1_stage_3), .Stage_5(control_unit_1_stage_5));
  LED led_1 (.in(control_unit_1_stage_1));
  LED led_2 (.in(control_unit_1_stage_2));
  LED led_3 (.in(control_unit_1_stage_3));
  LED led_4 (.in(control_unit_1_stage_4));
  LED led_5 (.in(control_unit_1_stage_5));

  // Other names for the same wires on the sheet: MemoryAddress[18:0] = {CS, Address}; Immediate[31:19] = {13{in_1}};
  //   Clear_PC = Clear_IR; Clear_RA = Clear_IR; Clear_Ram = Clear_IR; Clear_RB = Clear_IR; Clear_RM = Clear_IR;
  //   Clear_RY = Clear_IR; Clear_RZ = Clear_IR; Load_Stage_Clk = Clear_IR

  // Notes on the sheet:
  //   Fetch
  //   IR
  //   contents of rom_1 (hex, n*v repeats v):
  //   80001 0 1231423
  //   IAG
  //   Inst. Decoder
  //   Control Unit
  //   Stage -1
  //   Stage -2
  //   Stage -3
  //   Stage -4
  //   Stage -5
endmodule

module Control_Unit (
  input  Load_Signal,
  input  Store_Signal,
  input  Move_Signal,
  input  Jump_Signal,
  input  Signal,
  input  Subtract_Signal,
  input  x_Signal,
  input  Signal_2,
  input  Clock,
  input  [2:0] Op_Code,
  input  Load_Stage_Clk,
  output En_IR,
  output Stage_5,
  output En_PC,
  output Stage_4,
  output Select_MUX_MA,
  output Stage_3,
  output Enable_MUX_MA,
  output Stage_2,
  output Enable_PCSet,
  output Stage_1,
  output Select_PCSet,
  output En_RA,
  output En_RB,
  output En_Select_RA,
  output En_Select_RB,
  output En_RZ,
  output [1:0] Select_ALU,
  output En_RM,
  output En_ALU,
  output Select_MUX_Y,
  output En_MUX_Y,
  output Load_Write_Ram,
  output Enable_to_MUX_Y,
  output En_RY,
  output En_Select_RC,
  output En_MUX_B,
  output Select_MUX_B
);

  wire and_4_out, and_9_out, and_12_out, and_13_out, and_14_out, and_15_out, not_1_out, or_1_out, or_2_out,
       or_3_out, or_6_out, or_7_out, or_8_out, or_9_out, or_11_out, or_12_out, or_14_out, or_16_out,
       or_17_out, shift_register_1_out;

  or or_1 (or_1_out, Load_Signal, Store_Signal, Move_Signal, Jump_Signal, Signal, Subtract_Signal, x_Signal, Signal_2);
  or or_2 (or_2_out, Load_Signal, Store_Signal, Move_Signal, Jump_Signal, Signal, Subtract_Signal, x_Signal, Signal_2);
  or or_3 (or_3_out, Load_Signal, Move_Signal, Signal, Subtract_Signal, x_Signal, Signal_2);
  and and_1 (En_IR, Stage_1, or_1_out);
  and and_2 (En_ALU, Stage_3, or_2_out);
  and and_3 (En_MUX_Y, Stage_4, or_3_out);
  or or_4 (Select_MUX_MA, En_IR, Stage_5);
  and and_4 (and_4_out, Stage_3, Jump_Signal);
  or or_5 (En_PC, and_4_out, En_IR);
  not not_1 (not_1_out, Load_Stage_Clk);
  and and_5 (Enable_to_MUX_Y, Stage_4, Load_Signal);
  or or_6 (or_6_out, Load_Signal, Move_Signal, Signal, Subtract_Signal, x_Signal, Signal_2);
  and and_6 (En_Select_RC, Stage_5, or_6_out);
  Shift_Register #(.length(5)) shift_register_1 (
    .shift(not_1_out), .in(shift_register_1_out), .clk(Clock), .out(shift_register_1_out),
    .load(Load_Stage_Clk), .d0(1'b1), .q0(Stage_1), .d1(1'b0), .q1(Stage_2), .d2(1'b0), .q2(Stage_3),
    .d3(1'b0), .q3(Stage_4), .d4(1'b0), .q4(Stage_5));  // open: clr
  and and_7 (Select_PCSet, Stage_1, or_7_out);
  or or_7 (or_7_out, Load_Signal, Store_Signal, Move_Signal, Signal, Subtract_Signal, x_Signal, Signal_2);
  // Probe on Select_ALU
  assign Select_ALU = Op_Code[1:0] & {2{Op_Code[2]}};  // AND_Gate and_8, 2 bits wide
  and and_9 (and_9_out, Stage_4, or_8_out);
  or or_8 (or_8_out, Load_Signal, Store_Signal);
  or or_9 (or_9_out, Load_Signal, Store_Signal, Move_Signal, Jump_Signal, Signal, Subtract_Signal, x_Signal, Signal_2);
  and and_10 (En_RM, Stage_3, Store_Signal);
  or or_10 (Enable_MUX_MA, Stage_1, Stage_5, and_9_out);
  and and_11 (En_RA, Stage_2, or_9_out);
  and and_12 (and_12_out, Stage_3, or_11_out);
  or or_11 (or_11_out, Signal, Subtract_Signal, x_Signal, Signal_2);
  and and_13 (and_13_out, Stage_3, or_12_out);
  or or_12 (or_12_out, Load_Signal, Store_Signal, Move_Signal, Jump_Signal, Signal, Subtract_Signal, x_Signal, Signal_2);
  or or_13 (En_RZ, and_12_out, and_13_out);
  or or_14 (or_14_out, Load_Signal, Store_Signal, Move_Signal, Signal, Subtract_Signal, x_Signal, Signal_2);
  and and_14 (and_14_out, Stage_3, Jump_Signal);
  and and_15 (and_15_out, Stage_1, or_14_out);
  or or_15 (Enable_PCSet, and_14_out, and_15_out);
  or or_16 (or_16_out, Load_Signal, Store_Signal, Move_Signal, Jump_Signal, Signal, Subtract_Signal, x_Signal, Signal_2);
  or or_17 (or_17_out, Load_Signal, Store_Signal);
  and and_16 (En_MUX_B, Stage_3, or_16_out);
  and and_17 (Select_MUX_B, Stage_3, or_17_out);

  assign En_RB = En_RA;
  assign En_RY = En_MUX_Y;
  assign En_Select_RA = En_RA;
  assign En_Select_RB = En_RA;
  assign Load_Write_Ram = Enable_to_MUX_Y;
  assign Select_MUX_Y = Enable_to_MUX_Y;

  // Other names for the same wires on the sheet: Signal_t = Signal_2
endmodule
